# Fritzing sketch Untitled Sketch (saved by Fritzing 0.9.3b)
perfboards: 1

parts:
  Part1 = BluePill  # not connected
  U1 = NodeMCU V3.0
  Part2 = Triple Axis Accelerometer Breakout - ADXL335  # not connected

nets:
  N1: U1.GND#6, U1.GND#13, U1.GND#16, U1.GND#33

custom parts:
  NodeMCU V3.0: ESP8266 based NodeMCU
